# Fritzing sketch Esq_Elet_Fritzing (saved by Fritzing 1.0.2b)
breadboards: 1

parts:
  R1 = Resistor [tolerance=±5% power=0.25W resistance=12k package=THT]
  R2 = Resistor [tolerance=±5% power=0.25W resistance=12k package=THT]
  D1 = Rectifier Diode [part_number=1N4004 package="300 mil [THT]"]
  part = LCD1602-I2C
  part_2 = Arduino Uno (Rev3)

nets:
  N1: R1.Pin_0, R2.Pin_0, part_2.A0, part_2.D2
  N2: R1.Pin_1, D1.cathode
  GND: R2.Pin_1, part.GND, part_2.GND
  VCC GF: D1.anode
  VCC: part.VCC, part_2.5V
  N3: part.SDA, part_2.A4/SDA
  N4: part.SCL, part_2.A5/SCL

custom parts:
  LCD1602-I2C: A standard character display, usually with 2x16 characters. Comes in many colors with LCM1602 IIC attached.
